# Fritzing sketch Alcohol_Sanitizer (saved by Fritzing 0.9.4)
breadboards: 1

parts:
  ESP1 = ESP32-DevkitC
  J1 = Basic Servo
  HC-SR04_Sensor_1 = HC-SR04 Ultrasonic Distance Sensor

nets:
  N1: ESP1.IO33, J1.pulse
  GND: ESP1.IO12, ESP1.GND, J1.gnd, HC-SR04_Sensor_1.ECHO, HC-SR04_Sensor_1.GND
  N2: ESP1.IO13, HC-SR04_Sensor_1.TRIG
  VCC: ESP1.5V, J1.vcc, HC-SR04_Sensor_1.VCC
